// Logisim project IE.circ as structural Verilog: 1 circuit, main circuit main
module main (
  input  A0_LSB,
  input  A1_MSB,
  output B0_LSB,
  output B1_MSB
);

  wire HALF_ADDER_carry, xor_1_out;

  halfAdder HALF_ADDER (.xi(A0_LSB), .yi(1'b1), .sum(B0_LSB), .carry(HALF_ADDER_carry));
  xor xor_1 (xor_1_out, HALF_ADDER_carry, A1_MSB);
  halfAdder HALF_ADDER_2 (.xi(xor_1_out), .yi(1'b1), .sum(B1_MSB));  // open: carry

  // Notes on the sheet:
  //   CONSTANT
  //   ~2(1) FOR -VE ONE
endmodule
