// Logisim project IET.circ as structural Verilog
module _4BitCounter (
  input  in_1
);

  wire clock_1_out, nand_1_out, Qa_q, Qb_q, Qc_q, Qd_q, xor_1_out, xor_2_out, xor_3_out, xor_4_out;

  Clock clock_1 (.out(clock_1_out));
  T_Flip_Flop #(.trigger("falling")) Qa (
    .clk(clock_1_out), .T(1'b1), .Q(Qa_q), .reset(nand_1_out));  // open: Qn, preset, en
  xor xor_1 (xor_1_out, in_1, Qa_q);
  T_Flip_Flop #(.trigger("falling")) Qb (
    .clk(xor_1_out), .T(1'b1), .Q(Qb_q), .reset(nand_1_out));  // open: Qn, preset, en
  xor xor_2 (xor_2_out, in_1, Qb_q);
  T_Flip_Flop #(.trigger("falling")) Qc (
    .clk(xor_2_out), .T(1'b1), .Q(Qc_q), .reset(nand_1_out));  // open: Qn, preset, en
  nand nand_1 (nand_1_out, xor_4_out, xor_2_out);
  xor xor_3 (xor_3_out, in_1, Qc_q);
  T_Flip_Flop #(.trigger("falling")) Qd (
    .clk(xor_3_out), .T(1'b1), .Q(Qd_q), .reset(nand_1_out));  // open: Qn, preset, en
  xor xor_4 (xor_4_out, in_1, Qd_q);
endmodule
