// Logisim project fullAdder.circ as structural Verilog
module halfAdder (
  input  xi,
  input  yi,
  output sum,
  output carry
);

  xor xor_1 (sum, xi, yi);
  and and_1 (carry, xi, yi);

  // Notes on the sheet:
  //   XOR gate
  //   AND gete
endmodule

module fullAdder (
  input  ai,
  input  bi,
  input  ci,
  output sum,
  output co
);

  wire halfadder_1_carry, halfadder_1_sum, halfadder_2_carry;

  halfAdder halfadder_1 (.xi(ai), .yi(bi), .sum(halfadder_1_sum), .carry(halfadder_1_carry));
  halfAdder halfadder_2 (.xi(halfadder_1_sum), .yi(ci), .sum(sum), .carry(halfadder_2_carry));
  or or_1 (co, halfadder_1_carry, halfadder_2_carry);

  // Notes on the sheet:
  //   Half Adder
  //   Half Adder
endmodule

module _4bitAdder (
  input  [3:0] a,
  input  [3:0] b,
  output [3:0] sum,
  output carry
);

  wire fulladder_1_co, fulladder_2_co, halfadder_1_carry;

  halfAdder halfadder_1 (.xi(a[0]), .yi(b[0]), .sum(sum[0]), .carry(halfadder_1_carry));
  fullAdder fulladder_1 (.ai(a[1]), .bi(b[1]), .ci(halfadder_1_carry), .sum(sum[1]), .co(fulladder_1_co));
  fullAdder fulladder_2 (.ai(a[2]), .bi(b[2]), .ci(fulladder_1_co), .sum(sum[2]), .co(fulladder_2_co));
  fullAdder fulladder_3 (.ai(a[3]), .bi(b[3]), .ci(fulladder_2_co), .sum(sum[3]), .co(carry));
endmodule

module BCD_Dec (
  input  b0,
  input  b1,
  input  b2,
  input  b3,
  output a,
  output b,
  output c,
  output d,
  output e,
  output f,
  output g
);

  wire and_1_out, and_2_out, and_3_out, and_4_out, and_5_out, and_6_out, and_7_out, and_8_out, and_9_out,
       and_10_out, and_11_out, and_12_out, and_13_out, and_14_out, and_15_out, and_16_out, not_1_out,
       not_2_out, not_3_out, not_4_out, not_5_out, not_6_out, not_7_out, not_8_out, not_9_out, not_10_out,
       not_11_out, not_12_out, not_13_out, not_14_out, not_15_out, not_16_out, not_17_out, not_18_out,
       not_19_out, not_20_out, not_21_out;

  not not_1 (not_1_out, b1);
  and and_1 (and_1_out, not_1_out, not_2_out);
  not not_2 (not_2_out, b3);
  and and_2 (and_2_out, b1, b3);
  not not_3 (not_3_out, b1);
  not not_4 (not_4_out, b2);
  and and_3 (and_3_out, not_4_out, not_5_out);
  not not_5 (not_5_out, b3);
  and and_4 (and_4_out, b2, b3);
  not not_6 (not_6_out, b2);
  or or_1 (c, not_6_out, b3, b1);
  not not_7 (not_7_out, b1);
  and and_5 (and_5_out, not_7_out, not_8_out);
  not not_8 (not_8_out, b3);
  not not_9 (not_9_out, b1);
  and and_6 (and_6_out, not_9_out, b2);
  and and_7 (and_7_out, b2, not_10_out);
  not not_10 (not_10_out, b3);
  and and_8 (and_8_out, b1, not_11_out, b3);
  not not_11 (not_11_out, b2);
  not not_12 (not_12_out, b1);
  and and_9 (and_9_out, not_12_out, not_13_out);
  not not_13 (not_13_out, b3);
  and and_10 (and_10_out, b2, not_14_out);
  not not_14 (not_14_out, b3);
  not not_15 (not_15_out, b2);
  and and_11 (and_11_out, not_15_out, not_16_out);
  not not_16 (not_16_out, b3);
  and and_12 (and_12_out, b1, not_17_out);
  not not_17 (not_17_out, b2);
  and and_13 (and_13_out, b1, not_18_out);
  not not_18 (not_18_out, b3);
  not not_19 (not_19_out, b1);
  and and_14 (and_14_out, not_19_out, b2);
  and and_15 (and_15_out, b1, not_20_out);
  not not_20 (not_20_out, b2);
  and and_16 (and_16_out, b1, not_21_out);
  not not_21 (not_21_out, b3);
  or or_2 (a, and_1_out, b2, and_2_out, b0);
  or or_3 (b, not_3_out, and_3_out, and_4_out);
  or or_4 (d, and_5_out, and_6_out, and_7_out, and_8_out, b0);
  or or_5 (e, and_9_out, and_10_out);
  or or_6 (f, and_11_out, and_12_out, and_13_out, b0);
  or or_7 (g, and_14_out, and_15_out, and_16_out, b0);
  _7_Segment_Display u_7_segment_display_1 (.g(g), .f(f), .a(a), .b(b), .e(e), .d(d), .c(c));  // open: dp
endmodule

module BCD_Dec2 (
  input  b0,
  input  b1,
  input  b2,
  input  b3,
  output a,
  output b,
  output c,
  output d,
  output e,
  output f,
  output g
);

  wire and_1_out, and_2_out, and_3_out, and_4_out, and_5_out, and_6_out, and_7_out, and_8_out, and_9_out,
       and_10_out, and_11_out, and_12_out, and_13_out, and_14_out, and_15_out, and_16_out, not_1_out,
       not_2_out, not_3_out, not_4_out, not_5_out, not_6_out, not_7_out, not_8_out, not_9_out, not_10_out,
       not_11_out, not_12_out, not_13_out, not_14_out, not_15_out, not_16_out, not_17_out, not_18_out,
       not_19_out, not_20_out, not_21_out;

  not not_1 (not_1_out, b1);
  and and_1 (and_1_out, not_1_out, not_2_out);
  not not_2 (not_2_out, b3);
  and and_2 (and_2_out, b1, b3);
  not not_3 (not_3_out, b1);
  not not_4 (not_4_out, b2);
  and and_3 (and_3_out, not_4_out, not_5_out);
  not not_5 (not_5_out, b3);
  and and_4 (and_4_out, b2, b3);
  not not_6 (not_6_out, b2);
  or or_1 (c, not_6_out, b3, b1);
  not not_7 (not_7_out, b1);
  and and_5 (and_5_out, not_7_out, not_8_out);
  not not_8 (not_8_out, b3);
  not not_9 (not_9_out, b1);
  and and_6 (and_6_out, not_9_out, b2);
  and and_7 (and_7_out, b2, not_10_out);
  not not_10 (not_10_out, b3);
  and and_8 (and_8_out, b1, not_11_out, b3);
  not not_11 (not_11_out, b2);
  not not_12 (not_12_out, b1);
  and and_9 (and_9_out, not_12_out, not_13_out);
  not not_13 (not_13_out, b3);
  and and_10 (and_10_out, b2, not_14_out);
  not not_14 (not_14_out, b3);
  not not_15 (not_15_out, b2);
  and and_11 (and_11_out, not_15_out, not_16_out);
  not not_16 (not_16_out, b3);
  and and_12 (and_12_out, b1, not_17_out);
  not not_17 (not_17_out, b2);
  and and_13 (and_13_out, b1, not_18_out);
  not not_18 (not_18_out, b3);
  not not_19 (not_19_out, b1);
  and and_14 (and_14_out, not_19_out, b2);
  and and_15 (and_15_out, b1, not_20_out);
  not not_20 (not_20_out, b2);
  and and_16 (and_16_out, b1, not_21_out);
  not not_21 (not_21_out, b3);
  or or_2 (a, and_1_out, b2, and_2_out, b0);
  or or_3 (b, not_3_out, and_3_out, and_4_out);
  or or_4 (d, and_5_out, and_6_out, and_7_out, and_8_out, b0);
  or or_5 (e, and_9_out, and_10_out);
  or or_6 (f, and_11_out, and_12_out, and_13_out, b0);
  or or_7 (g, and_14_out, and_15_out, and_16_out, b0);
endmodule

module BCD_Dec3 (
  input  b0,
  input  b1,
  input  b2,
  input  b3,
  output a,
  output b,
  output c,
  output d,
  output e,
  output f,
  output g
);

  wire and_1_out, and_2_out, and_3_out, and_4_out, and_5_out, and_6_out, and_7_out, and_8_out, and_9_out,
       and_10_out, and_11_out, and_12_out, and_13_out, and_14_out, and_15_out, and_16_out, not_1_out,
       not_2_out, not_3_out, not_4_out, not_5_out, not_6_out, not_7_out, not_8_out, not_9_out, not_10_out,
       not_11_out, not_12_out, not_13_out, not_14_out, not_15_out, not_16_out, not_17_out, not_18_out,
       not_19_out, not_20_out, not_21_out;

  not not_1 (not_1_out, b1);
  and and_1 (and_1_out, not_1_out, not_2_out);
  not not_2 (not_2_out, b3);
  and and_2 (and_2_out, b1, b3);
  not not_3 (not_3_out, b1);
  not not_4 (not_4_out, b2);
  and and_3 (and_3_out, not_4_out, not_5_out);
  not not_5 (not_5_out, b3);
  and and_4 (and_4_out, b2, b3);
  not not_6 (not_6_out, b2);
  or or_1 (c, not_6_out, b3, b1);
  not not_7 (not_7_out, b1);
  and and_5 (and_5_out, not_7_out, not_8_out);
  not not_8 (not_8_out, b3);
  not not_9 (not_9_out, b1);
  and and_6 (and_6_out, not_9_out, b2);
  and and_7 (and_7_out, b2, not_10_out);
  not not_10 (not_10_out, b3);
  not not_11 (not_11_out, b2);
  and and_8 (and_8_out, b1, not_11_out, b3);
  not not_12 (not_12_out, b1);
  and and_9 (and_9_out, not_12_out, not_13_out);
  not not_13 (not_13_out, b3);
  and and_10 (and_10_out, b2, not_14_out);
  not not_14 (not_14_out, b3);
  not not_15 (not_15_out, b2);
  and and_11 (and_11_out, not_15_out, not_16_out);
  not not_16 (not_16_out, b3);
  and and_12 (and_12_out, b1, not_17_out);
  not not_17 (not_17_out, b2);
  and and_13 (and_13_out, b1, not_18_out);
  not not_18 (not_18_out, b3);
  not not_19 (not_19_out, b1);
  and and_14 (and_14_out, not_19_out, b2);
  and and_15 (and_15_out, b1, not_20_out);
  not not_20 (not_20_out, b2);
  and and_16 (and_16_out, b1, not_21_out);
  not not_21 (not_21_out, b3);
  or or_2 (a, and_1_out, b2, and_2_out, b0);
  or or_3 (b, not_3_out, and_3_out, and_4_out);
  or or_4 (d, and_5_out, and_6_out, and_7_out, and_8_out, b0);
  or or_5 (e, and_9_out, and_10_out);
  or or_6 (f, and_11_out, and_12_out, and_13_out, b0);
  or or_7 (g, and_14_out, and_15_out, and_16_out, b0);
endmodule
