// Logisim project halfAdder.circ as structural Verilog
module halfAdder (
  input  xi,
  input  yi,
  output sum,
  output count
);

  xor xor_1 (sum, xi, yi);
  and and_1 (count, xi, yi);
endmodule

module fullAdder (
  input  ai,
  input  bi,
  input  ci,
  output sum,
  output co
);

  wire halfadder_1_count, halfadder_2_count, halfadder_2_sum;

  halfAdder halfadder_1 (.xi(halfadder_2_sum), .yi(ci), .sum(sum), .count(halfadder_1_count));
  halfAdder halfadder_2 (.xi(ai), .yi(bi), .sum(halfadder_2_sum), .count(halfadder_2_count));
  or or_1 (co, halfadder_1_count, halfadder_2_count);
endmodule
