// Logisim project BCD_ADDER_4_BIT.circ as structural Verilog
module adder (
  input  [3:0] a,
  input  [3:0] b,
  output a_2,
  output [3:0] sum,
  output b_2,
  output carry,
  output c,
  output d,
  output e,
  output f,
  output g
);

  wire and_1_out, and_2_out, and_3_out, and_4_out, and_5_out, and_6_out, and_7_out, and_8_out, and_9_out,
       and_10_out, and_11_out, and_12_out, and_13_out, and_14_out, and_15_out, and_16_out, fulladder_1_co,
       fulladder_2_co, halfadder_1_carry, not_1_out, not_2_out, not_3_out, not_4_out, not_5_out, not_6_out,
       not_7_out, not_8_out, not_9_out, not_10_out, not_11_out, not_12_out, not_13_out, not_14_out,
       not_15_out, not_16_out, not_17_out, not_18_out, not_19_out, not_20_out, not_21_out;

  halfAdder halfadder_1 (.xi(a[0]), .yi(b[0]), .sum(sum[0]), .carry(halfadder_1_carry));
  fullAdder fulladder_1 (.ai(a[1]), .bi(b[1]), .ci(halfadder_1_carry), .sum(sum[1]), .co(fulladder_1_co));
  fullAdder fulladder_2 (.ai(a[2]), .bi(b[2]), .ci(fulladder_1_co), .sum(sum[2]), .co(fulladder_2_co));
  fullAdder fulladder_3 (.ai(a[3]), .bi(b[3]), .ci(fulladder_2_co), .sum(sum[3]), .co(carry));
  not not_1 (not_1_out, sum[2]);
  not not_2 (not_2_out, sum[0]);
  not not_3 (not_3_out, sum[1]);
  not not_4 (not_4_out, sum[0]);
  not not_5 (not_5_out, sum[1]);
  not not_6 (not_6_out, sum[2]);
  not not_7 (not_7_out, sum[0]);
  not not_8 (not_8_out, sum[2]);
  not not_9 (not_9_out, sum[0]);
  not not_10 (not_10_out, sum[1]);
  not not_11 (not_11_out, sum[2]);
  not not_12 (not_12_out, sum[0]);
  not not_13 (not_13_out, sum[0]);
  not not_14 (not_14_out, sum[1]);
  not not_15 (not_15_out, sum[0]);
  not not_16 (not_16_out, sum[1]);
  not not_17 (not_17_out, sum[0]);
  not not_18 (not_18_out, sum[2]);
  not not_19 (not_19_out, sum[1]);
  not not_20 (not_20_out, sum[0]);
  and and_1 (and_1_out, not_1_out, not_2_out);
  and and_2 (and_2_out, sum[2], sum[0]);
  not not_21 (not_21_out, sum[2]);
  and and_3 (and_3_out, not_3_out, not_4_out);
  or or_1 (b_2, not_21_out, and_3_out, and_4_out);
  and and_4 (and_4_out, sum[1], sum[0]);
  or or_2 (c, not_5_out, sum[0], sum[2]);
  and and_5 (and_5_out, not_6_out, not_7_out);
  and and_6 (and_6_out, not_8_out, sum[1]);
  and and_7 (and_7_out, sum[1], not_9_out);
  and and_8 (and_8_out, sum[2], not_10_out, sum[0]);
  and and_9 (and_9_out, not_11_out, not_12_out);
  or or_3 (e, and_9_out, and_10_out);
  and and_10 (and_10_out, sum[1], not_13_out);
  and and_11 (and_11_out, not_14_out, not_15_out);
  and and_12 (and_12_out, sum[2], not_16_out);
  and and_13 (and_13_out, sum[2], not_17_out);
  and and_14 (and_14_out, not_18_out, sum[1]);
  and and_15 (and_15_out, sum[2], not_19_out);
  and and_16 (and_16_out, sum[2], not_20_out);
  or or_4 (a_2, and_1_out, sum[1], and_2_out, sum[3]);
  or or_5 (d, and_5_out, and_6_out, and_7_out, and_8_out, sum[3]);
  or or_6 (f, and_11_out, and_12_out, and_13_out, sum[3]);
  or or_7 (g, and_14_out, and_15_out, and_16_out, sum[3]);
  _7_Segment_Display u_7_segment_display_1 (.g(g), .f(f), .a(a_2), .b(b_2), .e(e), .d(d), .c(c));  // open: dp

  // Notes on the sheet:
  //   4 BIT ADDER
  //   BCD TO SEVEN SEGMENT DECODER
endmodule
