// Logisim project MAJORITY_FUNCTION.circ as structural Verilog
module SENSOR (
  input  A,
  input  B,
  input  C,
  input  D,
  output R,
  output G
);

  wire and_1_out, and_2_out, and_3_out, and_4_out, and_5_out, and_6_out, and_7_out, and_8_out, and_9_out,
       and_10_out, not_1_out, not_2_out, not_3_out, not_4_out, not_5_out, not_6_out, not_7_out, not_8_out,
       not_9_out, not_10_out, not_11_out, not_12_out;

  and and_1 (and_1_out, C, D);
  and and_2 (and_2_out, B, D);
  and and_3 (and_3_out, B, C);
  and and_4 (and_4_out, A, D);
  and and_5 (and_5_out, A, C);
  and and_6 (and_6_out, A, B);
  not not_1 (not_1_out, A);
  not not_2 (not_2_out, B);
  not not_3 (not_3_out, C);
  not not_4 (not_4_out, A);
  not not_5 (not_5_out, B);
  not not_6 (not_6_out, D);
  not not_7 (not_7_out, A);
  not not_8 (not_8_out, C);
  not not_9 (not_9_out, D);
  not not_10 (not_10_out, B);
  not not_11 (not_11_out, C);
  not not_12 (not_12_out, D);
  LED led_1 (.in(R));
  or or_1 (R, and_1_out, and_2_out, and_3_out, and_4_out, and_5_out, and_6_out);
  and and_7 (and_7_out, not_1_out, not_2_out, not_3_out, D);
  and and_8 (and_8_out, not_4_out, not_5_out, C, not_6_out);
  and and_9 (and_9_out, not_7_out, B, not_8_out, not_9_out);
  and and_10 (and_10_out, A, not_10_out, not_11_out, not_12_out);
  or or_2 (G, and_7_out, and_8_out, and_9_out, and_10_out);
  LED led_2 (.in(G));
endmodule
