// Logisim project question1.circ as structural Verilog
module binToGrey (
  input  B3,
  input  B2,
  input  B1,
  input  B0,
  output G3,
  output G2,
  output G1,
  output G0
);

  xor xor_1 (G2, B3, B2);
  xor xor_2 (G1, B2, B1);
  xor xor_3 (G0, B1, B0);

  assign G3 = B3;

  // Notes on the sheet:
  //   MSB
endmodule

module greyTobin (
  input  G3,
  input  G2,
  input  G1,
  input  G0,
  output B3,
  output B2,
  output B1,
  output B0
);

  xor xor_1 (B2, G3, G2);
  xor xor_2 (B1, B2, G1);
  xor xor_3 (B0, B1, G0);

  assign B3 = G3;

  // Notes on the sheet:
  //   MSB
endmodule
