// Logisim project question3.circ as structural Verilog
module a_1 (
  input  A,
  input  B,
  input  C,
  input  D,
  output F1
);

  wire decoder_1_out11, decoder_1_out12, decoder_1_out13, decoder_1_out14, decoder_1_out15;

  Decoder #(.select(4), .enable("false")) decoder_1 (
    .out11(decoder_1_out11), .out12(decoder_1_out12), .out13(decoder_1_out13), .out14(decoder_1_out14),
    .out15(decoder_1_out15), .sel({A, B, C, D}));  // open: out0, out1, out2, out3, out4, out5, out6, out7, out8, out9, out10
  or or_1 (F1, decoder_1_out11, decoder_1_out12, decoder_1_out13, decoder_1_out14, decoder_1_out15);
endmodule

module b_1 (
  input  A,
  input  B,
  input  C,
  input  D,
  output F2
);

  wire decoder_1_out3, decoder_1_out7, decoder_1_out11, decoder_1_out12, decoder_1_out13, decoder_1_out15;

  Decoder #(.select(4), .enable("false")) decoder_1 (
    .out3(decoder_1_out3), .out7(decoder_1_out7), .out11(decoder_1_out11), .out12(decoder_1_out12),
    .out13(decoder_1_out13), .out15(decoder_1_out15), .sel({A, B, C, D}));  // open: out0, out1, out2, out4, out5, out6, out8, out9, out10, out14
  or or_1 (F2, decoder_1_out3, decoder_1_out7, decoder_1_out11, decoder_1_out12, decoder_1_out13, decoder_1_out15);
endmodule

module c_1 (
  input  A,
  input  B,
  input  C,
  input  D,
  output F3
);

  wire decoder_1_out3, decoder_1_out7, decoder_1_out12, decoder_1_out13, decoder_1_out14, decoder_1_out15;

  Decoder #(.select(4), .enable("false")) decoder_1 (
    .out3(decoder_1_out3), .out7(decoder_1_out7), .out12(decoder_1_out12), .out13(decoder_1_out13),
    .out14(decoder_1_out14), .out15(decoder_1_out15), .sel({A, B, C, D}));  // open: out0, out1, out2, out4, out5, out6, out8, out9, out10, out11
  or or_1 (F3, decoder_1_out3, decoder_1_out7, decoder_1_out12, decoder_1_out13, decoder_1_out14, decoder_1_out15);
endmodule

module a_2 (
  input  D,
  input  C,
  input  A,
  input  B,
  output F1
);

  wire and_1_out;

  and and_1 (and_1_out, D, A, C);
  Multiplexer #(.select(2), .enable("false")) multiplexer_1 (
    .in0(1'b0), .in1(1'b0), .in2(and_1_out), .in3(1'b1), .out(F1), .sel({A, B}));
endmodule

module b_2 (
  input  A,
  input  B,
  input  C,
  input  D,
  output F2
);

  wire and_1_out;

  and and_1 (and_1_out, A, B);
  Multiplexer #(.select(2), .enable("false")) multiplexer_1 (
    .in0(and_1_out), .in1(and_1_out), .in2(1'b0), .in3(1'b1), .out(F2), .sel({C, D}));
endmodule

module c_2 (
  input  C,
  input  D,
  input  A,
  input  B,
  output F3
);

  wire and_1_out;

  and and_1 (and_1_out, C, D);
  Multiplexer #(.select(2), .enable("false")) multiplexer_1 (
    .in0(and_1_out), .in1(and_1_out), .in2(1'b0), .in3(1'b1), .out(F3), .sel({A, B}));
endmodule
