// Logisim project question4.circ as structural Verilog: 1 circuit, main circuit main
module main (
  input  Q,
  input  R,
  input  S,
  input  T,
  input  A,
  input  B,
  input  C,
  input  D,
  output F
);

  wire and_1_out, and_2_out, not_1_out, not_2_out, not_3_out, or_1_out, or_2_out;

  not not_1 (not_1_out, R);
  not not_2 (not_2_out, S);
  or or_1 (or_1_out, not_1_out, S);
  not not_3 (not_3_out, Q);
  or or_2 (or_2_out, not_3_out, T);
  and and_1 (and_1_out, R, Q);
  and and_2 (and_2_out, not_2_out, T);
  Multiplexer #(.select(4), .enable("false")) multiplexer_1 (
    .in0(or_1_out), .in1(1'b1), .in2(1'b0), .in3(or_2_out), .in4(1'b0), .in5(1'b0), .in6(1'b0), .in7(1'b1),
    .in8(1'b1), .in9(1'b1), .in10(1'b0), .in11(1'b1), .in12(1'b0), .in13(and_1_out), .in14(1'b0),
    .in15(and_2_out), .out(F), .sel({A, B, C, D}));
endmodule
