// Logisim project question5 (1).circ as structural Verilog
module _8bit (
  input  A7,
  input  A6,
  input  A5,
  input  A4,
  input  A3,
  input  A2,
  input  A1,
  input  A0,
  input  SUB,
  input  B7,
  input  B6,
  input  B5,
  input  B4,
  input  B3,
  input  B2,
  input  B1,
  input  B0,
  output C_OUT,
  output S7,
  output S6,
  output S5,
  output S4,
  output S3,
  output S1,
  output out_25,
  output S0
);

  wire [7:0] xor_8_out;

  xor xor_1 (xor_8_out[7], SUB, A7);
  xor xor_2 (xor_8_out[6], SUB, A6);
  xor xor_3 (xor_8_out[5], SUB, A5);
  xor xor_4 (xor_8_out[4], SUB, A4);
  xor xor_5 (xor_8_out[3], SUB, A3);
  xor xor_6 (xor_8_out[2], SUB, A2);
  xor xor_7 (xor_8_out[1], SUB, A1);
  xor xor_8 (xor_8_out[0], SUB, A0);
  Adder adder_1 (
    .a(xor_8_out), .b({B7, B6, B5, B4, B3, B2, B1, B0}), .out({S7, S6, S5, S4, S3, S1, out_25, S0}),
    .cin(SUB), .cout(C_OUT));

  // Notes on the sheet:
  //   IF SUB = 1
  //   SUBTRACTION USING ~2
endmodule

module _4bit (
  input  A3,
  input  A2,
  input  A1,
  input  A0,
  input  SUB,
  input  B3,
  input  B2,
  input  B1,
  input  B0,
  output C_OUT,
  output S3,
  output S2,
  output S1,
  output S0
);

  wire [3:0] xor_3_out;

  xor xor_1 (xor_3_out[2], SUB, A2);
  xor xor_2 (xor_3_out[3], SUB, A3);
  xor xor_3 (xor_3_out[0], SUB, A0);
  xor xor_4 (xor_3_out[1], SUB, A1);
  Adder #(.width(4)) adder_1 (.a(xor_3_out), .b({B3, B2, B1, B0}), .out({S3, S2, S1, S0}), .cin(SUB), .cout(C_OUT));
endmodule
