// Logisim project question5.circ as structural Verilog
module _8bit (
  input  in_1,
  input  in_2,
  input  in_3,
  input  in_4,
  input  in_5,
  input  in_6,
  input  in_7,
  input  in_8,
  input  in_9,
  input  in_10,
  input  in_11,
  input  in_12,
  input  in_13,
  input  in_14,
  input  in_15,
  input  in_16,
  input  in_17,
  output out_18,
  output out_19,
  output out_20,
  output out_21,
  output out_22,
  output out_23,
  output out_24,
  output out_25,
  output out_26
);

  wire adder_1_cout;
  wire [3:0] xor_2_out, xor_5_out;

  xor xor_1 (xor_2_out[1], in_9, in_2);
  xor xor_2 (xor_2_out[0], in_9, in_1);
  xor xor_3 (xor_2_out[3], in_9, in_4);
  xor xor_4 (xor_2_out[2], in_9, in_3);
  Adder #(.width(4)) adder_1 (
    .a(xor_5_out), .b({in_17, in_16, in_15, in_14}), .out({out_26, out_25, out_24, out_23}), .cin(in_9),
    .cout(adder_1_cout));
  xor xor_5 (xor_5_out[0], in_9, in_5);
  xor xor_6 (xor_5_out[2], in_9, in_7);
  xor xor_7 (xor_5_out[1], in_9, in_6);
  xor xor_8 (xor_5_out[3], in_9, in_8);
  Adder #(.width(4)) adder_2 (
    .a(xor_2_out), .b({in_13, in_12, in_11, in_10}), .out({out_22, out_21, out_20, out_19}),
    .cin(adder_1_cout), .cout(out_18));
endmodule

module _4bit (
  input  in_1,
  input  in_2,
  input  in_3,
  input  in_4,
  input  in_5,
  input  in_6,
  input  in_7,
  input  in_8,
  input  in_9,
  output out_10,
  output out_11,
  output out_12,
  output out_13,
  output out_14
);

  wire [3:0] xor_4_out;

  xor xor_1 (xor_4_out[2], in_5, in_2);
  xor xor_2 (xor_4_out[3], in_5, in_1);
  xor xor_3 (xor_4_out[1], in_5, in_3);
  xor xor_4 (xor_4_out[0], in_5, in_4);
  Adder #(.width(4)) adder_1 (
    .a(xor_4_out), .b({in_6, in_7, in_8, in_9}), .out({out_11, out_12, out_13, out_14}), .cin(in_5),
    .cout(out_10));
endmodule
