// Logisim project question1.circ as structural Verilog
module singledigbcd (
  input  in_1,
  input  [3:0] in_2,
  input  [3:0] in_3,
  output [3:0] out_4,
  output [3:0] out_5,
  output out_6
);

  wire adder_1_cout, adder_2_cout, and_1_out, and_2_out, bcd_decoder_1_a, bcd_decoder_1_b, bcd_decoder_1_c,
       bcd_decoder_1_d, bcd_decoder_1_e, bcd_decoder_1_f, bcd_decoder_1_g;
  wire [2:2] or_1_out;

  Adder #(.width(4)) adder_1 (.a(in_2), .b(in_3), .out(out_4), .cin(in_1), .cout(adder_1_cout));
  and and_1 (and_1_out, out_4[3], out_4[1]);
  and and_2 (and_2_out, out_4[3], out_4[2]);
  or or_1 (or_1_out[2], adder_1_cout, and_2_out, and_1_out);
  Adder #(.width(4)) adder_2 (
    .a(out_4), .b({1'b0, {2{or_1_out[2]}}, 1'b0}), .out(out_5), .cout(adder_2_cout));  // open: cin
  or or_2 (out_6, adder_1_cout, adder_2_cout);
  bcd_decoder bcd_decoder_1 (
    .x1(out_5[3]), .x2(out_5[2]), .x3(out_5[1]), .x4(out_5[0]), .a(bcd_decoder_1_a), .b(bcd_decoder_1_b),
    .c(bcd_decoder_1_c), .d(bcd_decoder_1_d), .e(bcd_decoder_1_e), .f(bcd_decoder_1_f), .g(bcd_decoder_1_g));
  _7_Segment_Display u_7_segment_display_1 (
    .g(bcd_decoder_1_g), .f(bcd_decoder_1_f), .a(bcd_decoder_1_a), .b(bcd_decoder_1_b), .e(bcd_decoder_1_e),
    .d(bcd_decoder_1_d), .c(bcd_decoder_1_c));  // open: dp
endmodule

module bcd_decoder (
  input  x1,
  input  x2,
  input  x3,
  input  x4,
  output a,
  output b,
  output c,
  output d,
  output e,
  output f,
  output g
);

  wire and_1_out, and_2_out, and_3_out, and_4_out, and_5_out, and_6_out, and_7_out, and_8_out, and_9_out,
       and_10_out, and_11_out, and_12_out, and_13_out, and_14_out, and_15_out, and_16_out, and_17_out,
       and_18_out, not_1_out, not_2_out, not_3_out, not_4_out, not_5_out, not_6_out, not_7_out, not_8_out,
       not_9_out, not_10_out, not_11_out, not_12_out, not_13_out, not_14_out, not_15_out, not_16_out,
       not_17_out, not_18_out, not_19_out, not_20_out, not_21_out, not_22_out, or_1_out, or_2_out, or_3_out,
       or_4_out, or_6_out, or_8_out, or_9_out, or_10_out, or_11_out, or_14_out, or_15_out;

  not not_1 (not_1_out, x2);
  and and_1 (and_1_out, not_1_out, not_2_out);
  not not_2 (not_2_out, x4);
  and and_2 (and_2_out, x2, x4);
  not not_3 (not_3_out, x2);
  not not_4 (not_4_out, x3);
  and and_3 (and_3_out, not_4_out, not_5_out);
  not not_5 (not_5_out, x4);
  not not_6 (not_6_out, x3);
  or or_1 (or_1_out, not_6_out, x4);
  not not_7 (not_7_out, x2);
  and and_4 (and_4_out, not_7_out, not_8_out);
  not not_8 (not_8_out, x4);
  not not_9 (not_9_out, x2);
  and and_5 (and_5_out, not_9_out, x3);
  not not_10 (not_10_out, x4);
  and and_6 (and_6_out, x2, not_11_out);
  not not_11 (not_11_out, x3);
  not not_12 (not_12_out, x2);
  and and_7 (and_7_out, not_12_out, not_13_out);
  not not_13 (not_13_out, x4);
  and and_8 (and_8_out, x3, not_14_out);
  not not_14 (not_14_out, x4);
  not not_15 (not_15_out, x3);
  and and_9 (and_9_out, not_15_out, not_16_out);
  not not_16 (not_16_out, x4);
  and and_10 (and_10_out, x2, not_17_out);
  not not_17 (not_17_out, x3);
  and and_11 (and_11_out, x2, not_18_out);
  not not_18 (not_18_out, x4);
  and and_12 (and_12_out, x1, not_19_out);
  not not_19 (not_19_out, x3);
  not not_20 (not_20_out, x2);
  and and_13 (and_13_out, not_20_out, x3);
  and and_14 (and_14_out, x2, not_21_out);
  not not_21 (not_21_out, x3);
  and and_15 (and_15_out, x2, not_22_out);
  not not_22 (not_22_out, x4);
  or or_2 (or_2_out, and_1_out, x3);
  or or_3 (or_3_out, and_2_out, x1);
  or or_4 (or_4_out, not_3_out, and_3_out);
  and and_16 (and_16_out, x3, x4);
  or or_5 (c, or_1_out, x2);
  or or_6 (or_6_out, and_4_out, and_5_out);
  and and_17 (and_17_out, x3, not_10_out);
  and and_18 (and_18_out, and_6_out, x4);
  or or_7 (e, and_7_out, and_8_out);
  or or_8 (or_8_out, and_9_out, and_10_out);
  or or_9 (or_9_out, and_11_out, and_12_out);
  or or_10 (or_10_out, and_13_out, and_14_out);
  or or_11 (or_11_out, and_15_out, x1);
  or or_12 (a, or_2_out, or_3_out);
  or or_13 (b, or_4_out, and_16_out);
  or or_14 (or_14_out, or_6_out, and_17_out);
  or or_15 (or_15_out, and_18_out, x1);
  or or_16 (f, or_8_out, or_9_out);
  or or_17 (g, or_10_out, or_11_out);
  or or_18 (d, or_14_out, or_15_out);
  _7_Segment_Display u_7_segment_display_1 (.g(g), .f(f), .a(a), .b(b), .e(e), .d(d), .c(c));  // open: dp
endmodule
