// Logisim project question3.circ as structural Verilog
module mod8up (
  output MSB,
  output out_2,
  output LSB
);

  wire Clock_out;

  Clock Clock (.out(Clock_out));
  J_K_Flip_Flop #(.trigger("falling")) JK_F_F1__ve_edge (
    .J(1'b1), .clk(Clock_out), .K(1'b1), .Q(LSB));  // open: Qn, preset, en, reset
  J_K_Flip_Flop #(.trigger("falling")) JK_F_F2__ve_edge (
    .J(1'b1), .clk(LSB), .K(1'b1), .Q(out_2));  // open: Qn, preset, en, reset
  J_K_Flip_Flop #(.trigger("falling")) JK_F_F3__ve_edge (
    .J(1'b1), .clk(out_2), .K(1'b1), .Q(MSB));  // open: Qn, preset, en, reset
endmodule

module mod8updown (
  input  MODE,
  input  in_2,
  output MSB,
  output out_4,
  output LSB
);

  wire Clock_out, JK_F_F1__ve_edge_qn, JK_F_F2__ve_edge_qn, multiplexer_1_out, multiplexer_2_out;

  Clock Clock (.out(Clock_out));
  J_K_Flip_Flop #(.trigger("falling")) JK_F_F1__ve_edge (
    .J(1'b1), .clk(Clock_out), .K(1'b1), .Q(LSB), .Qn(JK_F_F1__ve_edge_qn), .reset(in_2));  // open: preset, en
  Multiplexer #(.enable("false")) multiplexer_1 (
    .in0(LSB), .in1(JK_F_F1__ve_edge_qn), .out(multiplexer_1_out), .sel(MODE));
  J_K_Flip_Flop #(.trigger("falling")) JK_F_F2__ve_edge (
    .J(1'b1), .clk(multiplexer_1_out), .K(1'b1), .Q(out_4), .Qn(JK_F_F2__ve_edge_qn), .reset(in_2));  // open: preset, en
  Multiplexer #(.enable("false")) multiplexer_2 (
    .in0(out_4), .in1(JK_F_F2__ve_edge_qn), .out(multiplexer_2_out), .sel(MODE));
  J_K_Flip_Flop #(.trigger("falling")) JK_F_F3__ve_edge (
    .J(1'b1), .clk(multiplexer_2_out), .K(1'b1), .Q(MSB), .reset(in_2));  // open: Qn, preset, en
endmodule

module _2_up (
  output out_1,
  output LSB
);

  wire Clock_out;

  Clock Clock (.out(Clock_out));
  J_K_Flip_Flop #(.trigger("falling")) JK_F_F1__ve_edge (
    .J(1'b1), .clk(Clock_out), .K(1'b1), .Q(LSB));  // open: Qn, preset, en, reset
  J_K_Flip_Flop #(.trigger("falling")) JK_F_F2__ve_edge (
    .J(1'b1), .clk(LSB), .K(1'b1), .Q(out_1));  // open: Qn, preset, en, reset
endmodule
