// Logisim project question4.circ as structural Verilog
module mod11 (
  output LSB,
  output out_2,
  output out_3,
  output MSB
);

  wire clock_1_out, RESET_out;

  Clock clock_1 (.out(clock_1_out));
  J_K_Flip_Flop #(.trigger("falling")) JK_F_F1__ve_edge (
    .J(1'b1), .clk(clock_1_out), .K(1'b1), .Q(LSB), .reset(RESET_out));  // open: Qn, preset, en
  and RESET (RESET_out, MSB, out_2, LSB);
  J_K_Flip_Flop #(.trigger("falling")) JK_F_F2__ve_edge (
    .J(1'b1), .clk(LSB), .K(1'b1), .Q(out_2), .reset(RESET_out));  // open: Qn, preset, en
  J_K_Flip_Flop #(.trigger("falling")) JK_F_F3__ve_edge (
    .J(1'b1), .clk(out_2), .K(1'b1), .Q(out_3), .reset(RESET_out));  // open: Qn, preset, en
  J_K_Flip_Flop #(.trigger("falling")) JK_F_F4__ve_edge (
    .J(1'b1), .clk(out_3), .K(1'b1), .Q(MSB), .reset(RESET_out));  // open: Qn, preset, en
endmodule
