// Logisim project question5.circ as structural Verilog: 2 circuits, main circuit main
module main (
  output MSB,
  output out_2,
  output LSB
);

  wire BCD_DECODER_a_2, BCD_DECODER_b_2, BCD_DECODER_c_2, BCD_DECODER_d_2, BCD_DECODER_e, BCD_DECODER_f,
       BCD_DECODER_g, Clock_out, D1_Rising_Edge_qn, D2_RISING_EDGE_qn, D3_RIDING_EDGE_qn, RESET_GATE_out;

  Clock Clock (.out(Clock_out));
  D_Flip_Flop D1_Rising_Edge (
    .clk(Clock_out), .D(D1_Rising_Edge_qn), .Q(LSB), .Qn(D1_Rising_Edge_qn), .reset(RESET_GATE_out));  // open: preset, en
  D_Flip_Flop D2_RISING_EDGE (
    .clk(D1_Rising_Edge_qn), .D(D2_RISING_EDGE_qn), .Q(out_2), .Qn(D2_RISING_EDGE_qn), .reset(RESET_GATE_out));  // open: preset, en
  and RESET_GATE (RESET_GATE_out, MSB, out_2);
  D_Flip_Flop D3_RIDING_EDGE (
    .clk(D2_RISING_EDGE_qn), .D(D3_RIDING_EDGE_qn), .Q(MSB), .Qn(D3_RIDING_EDGE_qn), .reset(RESET_GATE_out));  // open: preset, en
  BCD BCD_DECODER (
    .D(1'b0), .C(MSB), .B(out_2), .A(LSB), .a_2(BCD_DECODER_a_2), .b_2(BCD_DECODER_b_2),
    .c_2(BCD_DECODER_c_2), .d_2(BCD_DECODER_d_2), .e(BCD_DECODER_e), .f(BCD_DECODER_f), .g(BCD_DECODER_g));
  _7_Segment_Display u_7_segment_display_1 (
    .g(BCD_DECODER_g), .f(BCD_DECODER_f), .a(BCD_DECODER_a_2), .b(BCD_DECODER_b_2), .e(BCD_DECODER_e),
    .d(BCD_DECODER_d_2), .c(BCD_DECODER_c_2));  // open: dp
endmodule

module BCD (
  input  D,
  input  C,
  input  B,
  input  A,
  output a_2,
  output b_2,
  output c_2,
  output d_2,
  output e,
  output f,
  output g
);

  wire and_1_out, and_2_out, and_3_out, and_4_out, and_5_out, and_6_out, and_7_out, and_8_out, and_9_out,
       and_10_out, and_11_out, and_12_out, and_13_out, and_14_out, and_15_out, and_16_out, not_1_out,
       not_2_out, not_3_out, not_4_out, not_5_out, not_6_out, not_7_out, not_8_out, not_9_out, not_10_out,
       not_11_out, not_12_out, not_13_out, not_14_out, not_15_out, not_16_out, not_17_out, not_18_out,
       not_19_out, not_20_out, not_21_out;

  not not_1 (not_1_out, C);
  and and_1 (and_1_out, not_1_out, not_2_out);
  not not_2 (not_2_out, A);
  and and_2 (and_2_out, C, A);
  not not_3 (not_3_out, C);
  not not_4 (not_4_out, B);
  and and_3 (and_3_out, not_4_out, not_5_out);
  not not_5 (not_5_out, A);
  and and_4 (and_4_out, B, A);
  not not_6 (not_6_out, B);
  or or_1 (c_2, not_6_out, A, C);
  not not_7 (not_7_out, C);
  and and_5 (and_5_out, not_7_out, not_8_out);
  not not_8 (not_8_out, A);
  not not_9 (not_9_out, C);
  and and_6 (and_6_out, not_9_out, B);
  and and_7 (and_7_out, B, not_10_out);
  not not_10 (not_10_out, A);
  not not_11 (not_11_out, B);
  and and_8 (and_8_out, C, not_11_out, A);
  not not_12 (not_12_out, C);
  and and_9 (and_9_out, not_12_out, not_13_out);
  not not_13 (not_13_out, A);
  and and_10 (and_10_out, B, not_14_out);
  not not_14 (not_14_out, A);
  not not_15 (not_15_out, B);
  and and_11 (and_11_out, not_15_out, not_16_out);
  not not_16 (not_16_out, A);
  and and_12 (and_12_out, C, not_17_out);
  not not_17 (not_17_out, B);
  and and_13 (and_13_out, C, not_18_out);
  not not_18 (not_18_out, A);
  not not_19 (not_19_out, C);
  and and_14 (and_14_out, not_19_out, B);
  and and_15 (and_15_out, C, not_20_out);
  not not_20 (not_20_out, B);
  and and_16 (and_16_out, C, not_21_out);
  not not_21 (not_21_out, A);
  or or_2 (a_2, and_1_out, B, and_2_out, D);
  or or_3 (b_2, not_3_out, and_3_out, and_4_out);
  or or_4 (d_2, and_5_out, and_6_out, and_7_out, and_8_out, D);
  or or_5 (e, and_9_out, and_10_out);
  or or_6 (f, and_11_out, and_12_out, and_13_out, D);
  or or_7 (g, and_14_out, and_15_out, and_16_out, D);
endmodule
