// Logisim project question6.circ as structural Verilog: 3 circuits, main circuit main
module main (
);

  wire n2_up_1_a0, n2_up_1_a1;

  _2_up u_2_up_1 (.A1(n2_up_1_a1), .A0(n2_up_1_a0));
endmodule

module _2_up (
  output A1,
  output A0
);

  wire Clock_out;

  Clock Clock (.out(Clock_out));
  J_K_Flip_Flop #(.trigger("falling")) JK_F_F1__ve_edge (
    .J(1'b1), .clk(Clock_out), .K(1'b1), .Q(A0));  // open: Qn, preset, en, reset
  J_K_Flip_Flop #(.trigger("falling")) JK_F_F2__ve_edge (
    .J(1'b1), .clk(A0), .K(1'b1), .Q(A1));  // open: Qn, preset, en, reset
endmodule

module _5_up (
  output A2,
  output A1,
  output A0
);

  wire and_1_out, Clock_out;

  Clock Clock (.out(Clock_out));
  J_K_Flip_Flop #(.trigger("falling")) JK_F_F1__ve_edge (
    .J(1'b1), .clk(Clock_out), .K(1'b1), .Q(A0), .reset(and_1_out));  // open: Qn, preset, en
  and and_1 (and_1_out, A2, A1);
  J_K_Flip_Flop #(.trigger("falling")) JK_F_F2__ve_edge (
    .J(1'b1), .clk(A0), .K(1'b1), .Q(A1), .reset(and_1_out));  // open: Qn, preset, en
  J_K_Flip_Flop #(.trigger("falling")) JK_F_F3__ve_edge (
    .J(1'b1), .clk(A1), .K(1'b1), .Q(A2), .reset(and_1_out));  // open: Qn, preset, en
endmodule
