// Logisim project Question1.circ as structural Verilog: 4 circuits, main circuit main
module main (
  output [2:0] out_1
);

  wire and_1_out, and_2_out, CLOCK_out, not_1_out, not_2_out, xor_1_out;

  Clock CLOCK (.out(CLOCK_out));
  and and_1 (and_1_out, out_1[0], out_1[1]);
  not not_1 (not_1_out, out_1[2]);
  xor xor_1 (xor_1_out, out_1[0], out_1[1]);
  D_Flip_Flop DA (.clk(CLOCK_out), .D(and_1_out), .Q(out_1[2]));  // open: Qn, preset, en, reset
  D_Flip_Flop DB (.clk(CLOCK_out), .D(xor_1_out), .Q(out_1[1]));  // open: Qn, preset, en, reset
  and and_2 (and_2_out, not_1_out, not_2_out);
  not not_2 (not_2_out, out_1[0]);
  D_Flip_Flop DC (.clk(CLOCK_out), .D(and_2_out), .Q(out_1[0]));  // open: Qn, preset, en, reset

  // Notes on the sheet:
  //   A
  //   B
  //   C
endmodule

module mod5Count (
  input  in_1,
  input  in_2,
  input  [2:0] in_3,
  output [2:0] out_4
);

  wire and_1_out, and_2_out, clock_1_out, multiplexer_1_out, multiplexer_2_out, multiplexer_3_out, xor_1_out,
       xor_2_out, xor_3_out;

  Clock clock_1 (.out(clock_1_out));
  xor xor_1 (xor_1_out, out_4[0], in_1);
  Multiplexer #(.enable("false")) multiplexer_1 (.in0(xor_1_out), .in1(in_3[0]), .out(multiplexer_1_out), .sel(in_2));
  D_Flip_Flop #(.trigger("falling")) d_ff_1 (
    .clk(clock_1_out), .D(multiplexer_1_out), .Q(out_4[0]));  // open: Qn, preset, en, reset
  xor xor_2 (xor_2_out, out_4[1], and_1_out);
  and and_1 (and_1_out, out_4[0], in_1);
  Multiplexer #(.enable("false")) multiplexer_2 (.in0(xor_2_out), .in1(in_3[1]), .out(multiplexer_2_out), .sel(in_2));
  D_Flip_Flop #(.trigger("falling")) d_ff_2 (
    .clk(clock_1_out), .D(multiplexer_2_out), .Q(out_4[1]));  // open: Qn, preset, en, reset
  xor xor_3 (xor_3_out, out_4[2], and_2_out);
  and and_2 (and_2_out, out_4[1], and_1_out);
  Multiplexer #(.enable("false")) multiplexer_3 (.in0(xor_3_out), .in1(in_3[2]), .out(multiplexer_3_out), .sel(in_2));
  D_Flip_Flop #(.trigger("falling")) d_ff_3 (
    .clk(clock_1_out), .D(multiplexer_3_out), .Q(out_4[2]));  // open: Qn, preset, en, reset
endmodule

module practicalClock (
  input  [3:0] in_1,
  input  [3:0] in_2
);

  wire bin2deci_1_a_2, bin2deci_1_b_2, bin2deci_1_c_2, bin2deci_1_d_2, bin2deci_1_e, bin2deci_1_f,
       bin2deci_1_g, bin2deci_2_a_2, bin2deci_2_b_2, bin2deci_2_c_2, bin2deci_2_d_2, bin2deci_2_e,
       bin2deci_2_f, bin2deci_2_g, button_1_out, button_2_out, clock_1_out, counter_1_carry, counter_2_carry;
  wire [3:0] counter_1_q, counter_2_q;

  Button button_1 (.out(button_1_out));
  Clock clock_1 (.out(clock_1_out));
  Counter #(.width(4), .max('h9), .trigger("falling")) counter_1 (
    .load(button_1_out), .D(in_2), .count(1'b1), .Q(counter_1_q), .carry(counter_1_carry), .clk(clock_1_out));  // open: clr
  Button button_2 (.out(button_2_out));
  Counter #(.width(4), .max('h5), .trigger("falling")) counter_2 (
    .load(button_2_out), .D(in_1), .count(1'b1), .Q(counter_2_q), .carry(counter_2_carry),
    .clk(counter_1_carry));  // open: clr
  bin2deci bin2deci_1 (
    .A(counter_1_q[3]), .B(counter_1_q[2]), .C(counter_1_q[1]), .D(counter_1_q[0]), .a_2(bin2deci_1_a_2),
    .b_2(bin2deci_1_b_2), .c_2(bin2deci_1_c_2), .d_2(bin2deci_1_d_2), .e(bin2deci_1_e), .f(bin2deci_1_f),
    .g(bin2deci_1_g));
  bin2deci bin2deci_2 (
    .A(counter_2_q[3]), .B(counter_2_q[2]), .C(counter_2_q[1]), .D(counter_2_q[0]), .a_2(bin2deci_2_a_2),
    .b_2(bin2deci_2_b_2), .c_2(bin2deci_2_c_2), .d_2(bin2deci_2_d_2), .e(bin2deci_2_e), .f(bin2deci_2_f),
    .g(bin2deci_2_g));
  _7_Segment_Display u_7_segment_display_1 (
    .g(bin2deci_1_g), .f(bin2deci_1_f), .a(bin2deci_1_a_2), .b(bin2deci_1_b_2), .e(bin2deci_1_e),
    .d(bin2deci_1_d_2), .c(bin2deci_1_c_2));  // open: dp
  _7_Segment_Display u_7_segment_display_2 (
    .g(bin2deci_2_g), .f(bin2deci_2_f), .a(bin2deci_2_a_2), .b(bin2deci_2_b_2), .e(bin2deci_2_e),
    .d(bin2deci_2_d_2), .c(bin2deci_2_c_2));  // open: dp
endmodule

module disp (
  input  [3:0] in_1
);

  wire bin2deci_1_a_2, bin2deci_1_b_2, bin2deci_1_c_2, bin2deci_1_d_2, bin2deci_1_e, bin2deci_1_f,
       bin2deci_1_g;

  bin2deci bin2deci_1 (
    .A(in_1[3]), .B(in_1[2]), .C(in_1[1]), .D(in_1[0]), .a_2(bin2deci_1_a_2), .b_2(bin2deci_1_b_2),
    .c_2(bin2deci_1_c_2), .d_2(bin2deci_1_d_2), .e(bin2deci_1_e), .f(bin2deci_1_f), .g(bin2deci_1_g));
  _7_Segment_Display u_7_segment_display_1 (
    .g(bin2deci_1_g), .f(bin2deci_1_f), .a(bin2deci_1_a_2), .b(bin2deci_1_b_2), .e(bin2deci_1_e),
    .d(bin2deci_1_d_2), .c(bin2deci_1_c_2));  // open: dp
endmodule
