// Logisim project Question2.circ as structural Verilog: 1 circuit, main circuit main
module main (
  input  in_1,
  input  MODE,
  output [3:0] OUTPUT
);

  wire and_1_out, and_2_out, CLOCK_out, j_k_ff_1_qn, j_k_ff_2_qn, j_k_ff_3_qn, multiplexer_1_out,
       multiplexer_2_out, multiplexer_3_out;

  Clock CLOCK (.out(CLOCK_out));
  J_K_Flip_Flop j_k_ff_1 (
    .J(in_1), .clk(CLOCK_out), .K(in_1), .Q(OUTPUT[0]), .Qn(j_k_ff_1_qn));  // open: preset, en, reset
  Multiplexer multiplexer_1 (.in0(OUTPUT[0]), .in1(j_k_ff_1_qn), .out(multiplexer_1_out), .sel(MODE));  // open: en
  J_K_Flip_Flop j_k_ff_2 (
    .J(multiplexer_1_out), .clk(CLOCK_out), .K(multiplexer_1_out), .Q(OUTPUT[1]), .Qn(j_k_ff_2_qn));  // open: preset, en, reset
  and and_1 (and_1_out, multiplexer_1_out, multiplexer_2_out);
  Multiplexer multiplexer_2 (.in0(OUTPUT[1]), .in1(j_k_ff_2_qn), .out(multiplexer_2_out), .sel(MODE));  // open: en
  J_K_Flip_Flop j_k_ff_3 (
    .J(and_1_out), .clk(CLOCK_out), .K(and_1_out), .Q(OUTPUT[2]), .Qn(j_k_ff_3_qn));  // open: preset, en, reset
  Multiplexer multiplexer_3 (.in0(OUTPUT[2]), .in1(j_k_ff_3_qn), .out(multiplexer_3_out), .sel(MODE));  // open: en
  and and_2 (and_2_out, and_1_out, multiplexer_3_out);
  J_K_Flip_Flop j_k_ff_4 (.J(and_2_out), .clk(CLOCK_out), .K(and_2_out), .Q(OUTPUT[3]));  // open: Qn, preset, en, reset
endmodule
