// Logisim project Question1.circ as structural Verilog
module JKFF (
  input  INPUT,
  output OUTPUT
);

  wire and_1_out, and_2_out, and_3_out, and_4_out, and_5_out, CLOCK_out, j_k_ff_1_q, j_k_ff_1_qn, j_k_ff_2_q,
       NEXT_STATE_DECODER_out, not_1_out, or_1_out;

  Clock CLOCK (.out(CLOCK_out));
  and and_1 (and_1_out, j_k_ff_2_q, INPUT);
  not not_1 (not_1_out, INPUT);
  J_K_Flip_Flop j_k_ff_1 (
    .J(NEXT_STATE_DECODER_out), .clk(CLOCK_out), .K(NEXT_STATE_DECODER_out), .Q(j_k_ff_1_q), .Qn(j_k_ff_1_qn));  // open: preset, en, reset
  J_K_Flip_Flop j_k_ff_2 (.J(or_1_out), .clk(CLOCK_out), .K(or_1_out), .Q(j_k_ff_2_q));  // open: Qn, preset, en, reset
  or NEXT_STATE_DECODER (NEXT_STATE_DECODER_out, and_1_out, and_3_out);
  and and_2 (and_2_out, j_k_ff_1_qn, INPUT);
  and and_3 (and_3_out, j_k_ff_1_q, j_k_ff_2_q);
  or or_1 (or_1_out, and_2_out, and_5_out, and_4_out);
  and and_4 (and_4_out, j_k_ff_1_qn, j_k_ff_2_q);
  and and_5 (and_5_out, j_k_ff_1_q, not_1_out);
  and and_6 (OUTPUT, INPUT, j_k_ff_1_q, j_k_ff_2_q);

  // Notes on the sheet:
  //   JK FF
endmodule

module DFF (
  input  INPUT,
  output OUTPUT
);

  wire and_1_out, and_2_out, and_3_out, and_4_out, and_5_out, CLOCK_out, d_ff_1_q, d_ff_1_qn, d_ff_2_q,
       d_ff_2_qn, not_1_out, or_1_out, or_2_out;

  Clock CLOCK (.out(CLOCK_out));
  and and_1 (and_1_out, d_ff_1_qn, d_ff_2_q, INPUT);
  not not_1 (not_1_out, INPUT);
  D_Flip_Flop #(.trigger("falling")) d_ff_1 (
    .clk(CLOCK_out), .D(or_1_out), .Q(d_ff_1_q), .Qn(d_ff_1_qn));  // open: preset, en, reset
  D_Flip_Flop #(.trigger("falling")) d_ff_2 (
    .clk(CLOCK_out), .D(or_2_out), .Q(d_ff_2_q), .Qn(d_ff_2_qn));  // open: preset, en, reset
  or or_1 (or_1_out, and_1_out, and_3_out);
  and and_2 (and_2_out, d_ff_1_qn, d_ff_2_qn, INPUT);
  and and_3 (and_3_out, d_ff_1_q, d_ff_2_qn);
  or or_2 (or_2_out, and_2_out, and_5_out, and_4_out);
  and and_4 (and_4_out, d_ff_1_q, d_ff_2_q, INPUT);
  and and_5 (and_5_out, d_ff_1_q, d_ff_2_qn, not_1_out);
  and and_6 (OUTPUT, INPUT, d_ff_1_q, d_ff_2_q);

  // Notes on the sheet:
  //   D FF
  //   NEXT STATE DECODER
endmodule
