// Logisim project Question4.circ as structural Verilog: 1 circuit, main circuit main
module main (
  input  Detector,
  output ST
);

  wire and_1_out, and_2_out, and_3_out, and_4_out, and_5_out, and_6_out, and_7_out, and_8_out, and_9_out,
       clock_1_out, counter_1_carry, counter_2_carry, decoder_1_out0, decoder_1_out1, decoder_1_out2,
       decoder_1_out3, not_1_out, not_2_out, not_3_out, not_4_out, not_5_out, not_6_out, not_7_out,
       not_8_out, not_9_out, not_10_out, or_1_out, or_2_out, or_3_out, or_4_out;
  wire [1:0] DFF_q;

  Clock clock_1 (.out(clock_1_out));
  D_Flip_Flop DFF (.clk(clock_1_out), .D(or_1_out), .Q(DFF_q[0]));  // open: Qn, preset, en, reset
  not not_1 (not_1_out, DFF_q[0]);
  not not_2 (not_2_out, counter_1_carry);
  not not_3 (not_3_out, DFF_q[0]);
  not not_4 (not_4_out, Detector);
  Counter #(.width(3), .max('h5)) counter_1 (
    .count(1'b1), .carry(counter_1_carry), .clk(clock_1_out));  // open: load, D, Q, clr
  and and_1 (and_1_out, not_1_out, counter_2_carry, Detector);
  and and_2 (and_2_out, DFF_q[0], not_2_out);
  and and_3 (and_3_out, DFF_q[1], not_3_out, not_4_out);
  D_Flip_Flop DFF_2 (.clk(clock_1_out), .D(or_3_out), .Q(DFF_q[1]));  // open: Qn, preset, en, reset
  Counter #(.width(3), .max('h7)) counter_2 (
    .count(1'b1), .carry(counter_2_carry), .clk(clock_1_out));  // open: load, D, Q, clr
  or or_1 (or_1_out, and_1_out, and_2_out, and_3_out);
  not not_5 (not_5_out, DFF_q[1]);
  not not_6 (not_6_out, DFF_q[0]);
  not not_7 (not_7_out, counter_1_carry);
  Decoder #(.select(2)) decoder_1 (
    .out0(decoder_1_out0), .out1(decoder_1_out1), .out2(decoder_1_out2), .out3(decoder_1_out3), .sel(DFF_q));  // open: en
  not not_8 (not_8_out, DFF_q[0]);
  not not_9 (not_9_out, DFF_q[0]);
  not not_10 (not_10_out, Detector);
  and and_4 (and_4_out, not_5_out, DFF_q[0], counter_1_carry);
  and and_5 (and_5_out, DFF_q[1], not_6_out);
  and and_6 (and_6_out, DFF_q[1], not_7_out);
  LED led_1 (.in(or_2_out));
  or or_2 (or_2_out, decoder_1_out3, decoder_1_out2);
  LED led_2 (.in(decoder_1_out1));
  LED led_3 (.in(decoder_1_out0));
  and and_7 (and_7_out, not_8_out, counter_2_carry, Detector);
  and and_8 (and_8_out, DFF_q[0], counter_1_carry);
  and and_9 (and_9_out, DFF_q[1], not_9_out, not_10_out);
  or or_3 (or_3_out, and_4_out, and_5_out, and_6_out);
  LED led_4 (.in(or_4_out));
  or or_4 (or_4_out, decoder_1_out0, decoder_1_out1);
  LED led_5 (.in(decoder_1_out3));
  LED led_6 (.in(decoder_1_out2));
  or or_5 (ST, and_7_out, and_8_out, and_9_out);

  // Notes on the sheet:
  //   D0
  //   D1
  //   Highway Traffic  Lights
  //   NITK Traffic Lights
endmodule
